# Fritzing sketch SimonSays (saved by Fritzing 0.9.5d)
breadboards: 1

parts:
  Bauteil1 = Adafruit T-Cobbler Plus [part_number="Adafruit #1989 and #2028"]
  Button = Pushbutton [package="[THT]"]
  R1 = Resistor [tolerance=±5% resistance=100 package=THT]
  R2 = Resistor [tolerance=±5% resistance=10k package=THT]
  LED1 = LED - 3mm [color="Red (633nm)" package="3 mm [THT]"]
  LED2 = LED - 3mm [color="Yellow (595nm)" package="3 mm [THT]"]
  Button1 = Pushbutton [package="[THT]"]
  R3 = Resistor [tolerance=±5% resistance=10k package=THT]
  R4 = Resistor [tolerance=±5% resistance=100 package=THT]
  LED3 = LED - 3mm [color="Green (555nm)" package="3 mm [THT]"]
  Button2 = Pushbutton [package="[THT]"]
  R5 = Resistor [tolerance=±5% resistance=10k package=THT]
  R6 = Resistor [tolerance=±5% resistance=100 package=THT]
  LED4 = LED - 3mm [color="Blue (430nm)" package="3 mm [THT]"]
  Button3 = Pushbutton [package="[THT]"]
  R7 = Resistor [tolerance=±5% resistance=10k package=THT]
  R8 = Resistor [tolerance=±5% resistance=100 package=THT]

nets:
  N1: Bauteil1.+3.3V, Button.Pin_3, Button.Pin_4, Button1.Pin_3, Button1.Pin_4, Button2.Pin_3, Button2.Pin_4, Button3.Pin_3, Button3.Pin_4
  N2: Bauteil1.GND, R2.Pin_1, LED1.cathode, LED2.cathode, R3.Pin_1, LED3.cathode, R5.Pin_1, LED4.cathode, R7.Pin_1
  N3: Bauteil1.GPIO6, Button3.Pin_1, Button3.Pin_2, R7.Pin_0
  N4: Bauteil1.GPIO13, Button2.Pin_1, Button2.Pin_2, R5.Pin_0
  N5: Bauteil1.GPIO19, Button1.Pin_1, Button1.Pin_2, R3.Pin_0
  N6: Bauteil1.GPIO26, Button.Pin_1, Button.Pin_2, R2.Pin_0
  N7: Bauteil1.GPIO12, R8.Pin_1
  N8: Bauteil1.GPIO16, R6.Pin_1
  N9: Bauteil1.GPIO20, R4.Pin_1
  N10: Bauteil1.GPIO21, R1.Pin_1
  N11: R1.Pin_0, LED1.anode
  N12: LED2.anode, R4.Pin_0
  N13: LED3.anode, R6.Pin_0
  N14: LED4.anode, R8.Pin_0

custom parts:
  Adafruit T-Cobbler Plus: The Raspberry Pi has landed on the Maker World like a 40-GPIO pinned, quad-USB ported, credit card sized bomb of DIY joy. And while you can use most of our great Model B accessories by hooking up our downgrade cable, its probably a good time to upgrade your set up and accessorize using all of the 40 pins. That's why we now carry the Assembled Adafruit Pi T-Cobbler Plus - Breakout + Cable for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
